// Logisim project 150116046_150116048_150117011.circ as structural Verilog: 13 circuits, main circuit main
module main (
);

  wire clock_1_out, cu_1_m1, cu_1_m3, cu_1_m4, cu_1_m5, cu_1_mem_r, cu_1_mem_w, cu_1_pc_w, cu_1_we,
       multiplexer_3_out, n18bitcomparator_1_eq_out, n18bitcomparator_1_ge_out, n18bitcomparator_1_gt_out,
       n18bitcomparator_1_le_out, n18bitcomparator_1_lt_out;
  wire [1:0] cu_1_alu_c, cu_1_m2;
  wire [2:0] cu_1_mcmp;
  wire [3:0] cu_1_dr, cu_1_src1, cu_1_src2;
  wire [9:0] bit_extender_1_out;
  wire [17:0] adder_1_out, adder_2_out, adder_3_out, alu_1_out_data, cu_1_adress, cu_1_adress_2, cu_1_imm,
       cu_1_jumpadress, multiplexer_1_out, multiplexer_2_out, multiplexer_4_out, multiplexer_5_out,
       multiplexer_6_out, multiplexer_7_out, PC_q, ram_1_data, regfile_1_output1, regfile_1_output2,
       rom_1_data;

  Register #(.width(18)) PC (.D(multiplexer_7_out), .en(cu_1_pc_w), .Q(PC_q), .clk(clock_1_out), .clr(1'b0));
  Clock clock_1 (.out(clock_1_out));
  ROM #(.addrWidth(18), .dataWidth(18)) rom_1 (.addr(PC_q), .data(rom_1_data), .sel(1'b1));
  RegFile regfile_1 (
    .SRC1(cu_1_src1), .Input(multiplexer_6_out), .SRC2(cu_1_src2), .DR(cu_1_dr), .WE(cu_1_we),
    .clk(clock_1_out), .Output1(regfile_1_output1), .Output2(regfile_1_output2));
  Adder #(.width(18)) adder_1 (.a(PC_q), .b(18'h1), .out(adder_1_out), .cin(1'b0));  // open: cout
  Adder #(.width(18)) adder_2 (.a(cu_1_adress_2), .b(adder_1_out), .out(adder_2_out), .cin(1'b0));  // open: cout
  Adder #(.width(18)) adder_3 (.a(cu_1_jumpadress), .b(adder_1_out), .out(adder_3_out), .cin(1'b0));  // open: cout
  CU cu_1 (
    .\input (rom_1_data), .clk(clock_1_out), .DR(cu_1_dr), .SRC1(cu_1_src1), .SRC2(cu_1_src2),
    .IMM(cu_1_imm), .ADRESS(cu_1_adress), .JUMPADRESS(cu_1_jumpadress), .ADRESS_2(cu_1_adress_2),
    .m1(cu_1_m1), .alu_c(cu_1_alu_c), .m3(cu_1_m3), .Mem_r(cu_1_mem_r), .Mem_w(cu_1_mem_w), .m5(cu_1_m5),
    .WE(cu_1_we), .m2(cu_1_m2), .m4(cu_1_m4), .pc_w(cu_1_pc_w), .mcmp(cu_1_mcmp));  // open: branch, pc_r
  Multiplexer #(.width(18), .enable("false")) multiplexer_1 (
    .in0(regfile_1_output2), .in1(cu_1_imm), .out(multiplexer_1_out), .sel(cu_1_m1));
  ALU alu_1 (.in1(regfile_1_output1), .in2(multiplexer_1_out), .operation(cu_1_alu_c), .out_data(alu_1_out_data));
  _18bitcomparator u_18bitcomparator_1 (
    .in2(regfile_1_output2), .in1(regfile_1_output1), .eq_out(n18bitcomparator_1_eq_out),
    .gt_out(n18bitcomparator_1_gt_out), .lt_out(n18bitcomparator_1_lt_out),
    .ge_out(n18bitcomparator_1_ge_out), .le_out(n18bitcomparator_1_le_out));
  Multiplexer #(.select(2), .width(18), .enable("false")) multiplexer_2 (
    .in0(alu_1_out_data), .in1(cu_1_adress), .in2(adder_3_out), .in3(multiplexer_4_out),
    .out(multiplexer_2_out), .sel(cu_1_m2));
  Multiplexer #(.select(3), .enable("false")) multiplexer_3 (
    .in0(n18bitcomparator_1_eq_out), .in1(n18bitcomparator_1_gt_out), .in2(n18bitcomparator_1_lt_out),
    .in3(n18bitcomparator_1_ge_out), .in4(n18bitcomparator_1_le_out), .out(multiplexer_3_out), .sel(cu_1_mcmp));  // open: in5, in6, in7
  Bit_Extender #(.in_width(18), .out_width(10)) bit_extender_1 (.in(multiplexer_2_out), .out(bit_extender_1_out));
  Multiplexer #(.width(18), .enable("false")) multiplexer_4 (
    .in0(adder_1_out), .in1(adder_2_out), .out(multiplexer_4_out), .sel(multiplexer_3_out));
  RAM #(.addrWidth(10), .dataWidth(18), .bus("separate")) ram_1 (
    .addr(bit_extender_1_out), .din(regfile_1_output1), .data(ram_1_data), .str(cu_1_mem_w), .sel(1'b1),
    .clk(clock_1_out), .ld(cu_1_mem_r), .clr(1'b0));
  Multiplexer #(.width(18), .enable("false")) multiplexer_5 (
    .in0(ram_1_data), .in1(multiplexer_2_out), .out(multiplexer_5_out), .sel(cu_1_m3));
  Multiplexer #(.width(18), .enable("false")) multiplexer_6 (
    .in0(multiplexer_5_out), .in1(adder_1_out), .out(multiplexer_6_out), .sel(cu_1_m4));
  Multiplexer #(.width(18), .enable("false")) multiplexer_7 (
    .in0(multiplexer_5_out), .in1(adder_1_out), .out(multiplexer_7_out), .sel(cu_1_m5));

  // Notes on the sheet:
  //   contents of rom_1 (hex, n*v repeats v):
  //   2c402 2c804 34805 8c48 1d4fd 1104c 26139 384b1 2d804 e50c 36003 3848e 2bffa 2dc08 2ec08 39ed3 164be
  //   1851c 38562 2048c 34406 3849d
  //   m1(src/imm)
  //   m2(alu/address)
  //   m3(mmd/m2)
  //   m4
  //   m5
endmodule

module RegisterFile (
  input  [3:0] SRC1,
  input  [17:0] Input,
  input  [3:0] SRC2,
  input  [3:0] DR,
  input  WE,
  input  clk,
  output [17:0] Output1,
  output [17:0] Output2
);

  wire and_1_out, and_2_out, and_3_out, and_4_out, and_5_out, and_6_out, and_7_out, and_8_out, and_9_out,
       and_10_out, and_11_out, and_12_out, and_13_out, and_14_out, and_15_out, and_16_out, decoder_1_out0,
       decoder_1_out1, decoder_1_out2, decoder_1_out3, decoder_1_out4, decoder_1_out5, decoder_1_out6,
       decoder_1_out7, decoder_1_out8, decoder_1_out9, decoder_1_out10, decoder_1_out11, decoder_1_out12,
       decoder_1_out13, decoder_1_out14, decoder_1_out15;
  wire [3:0] undriven, undriven_2;
  wire [17:0] register_1_q, register_2_q, register_3_q, register_4_q, register_5_q, register_6_q,
       register_7_q, register_8_q, register_9_q, register_10_q, register_11_q, register_12_q, register_13_q,
       register_14_q, register_15_q, register_16_q;

  Decoder #(.select(4), .enable("false")) decoder_1 (
    .out0(decoder_1_out0), .out1(decoder_1_out1), .out2(decoder_1_out2), .out3(decoder_1_out3),
    .out4(decoder_1_out4), .out5(decoder_1_out5), .out6(decoder_1_out6), .out7(decoder_1_out7),
    .out8(decoder_1_out8), .out9(decoder_1_out9), .out10(decoder_1_out10), .out11(decoder_1_out11),
    .out12(decoder_1_out12), .out13(decoder_1_out13), .out14(decoder_1_out14), .out15(decoder_1_out15),
    .sel(DR));
  and and_1 (and_1_out, decoder_1_out0, WE);
  and and_2 (and_2_out, decoder_1_out1, WE);
  and and_3 (and_3_out, decoder_1_out2, WE);
  and and_4 (and_4_out, decoder_1_out3, WE);
  and and_5 (and_5_out, decoder_1_out4, WE);
  and and_6 (and_6_out, decoder_1_out5, WE);
  and and_7 (and_7_out, decoder_1_out6, WE);
  and and_8 (and_8_out, decoder_1_out7, WE);
  and and_9 (and_9_out, decoder_1_out8, WE);
  and and_10 (and_10_out, decoder_1_out9, WE);
  and and_11 (and_11_out, decoder_1_out10, WE);
  and and_12 (and_12_out, decoder_1_out11, WE);
  and and_13 (and_13_out, decoder_1_out12, WE);
  and and_14 (and_14_out, decoder_1_out13, WE);
  and and_15 (and_15_out, decoder_1_out14, WE);
  and and_16 (and_16_out, decoder_1_out15, WE);
  Register #(.width(18)) register_1 (.D(Input), .en(and_1_out), .Q(register_1_q), .clk(clk), .clr(1'b0));
  Register #(.width(18)) register_2 (.D(Input), .en(and_2_out), .Q(register_2_q), .clk(clk), .clr(1'b0));
  Register #(.width(18)) register_3 (.D(Input), .en(and_3_out), .Q(register_3_q), .clk(clk), .clr(1'b0));
  Register #(.width(18)) register_4 (.D(Input), .en(and_4_out), .Q(register_4_q), .clk(clk), .clr(1'b0));
  Register #(.width(18)) register_5 (.D(Input), .en(and_5_out), .Q(register_5_q), .clk(clk), .clr(1'b0));
  Register #(.width(18)) register_6 (.D(Input), .en(and_6_out), .Q(register_6_q), .clk(clk), .clr(1'b0));
  Register #(.width(18)) register_7 (.D(Input), .en(and_7_out), .Q(register_7_q), .clk(clk), .clr(1'b0));
  Register #(.width(18)) register_8 (.D(Input), .en(and_8_out), .Q(register_8_q), .clk(clk), .clr(1'b0));
  Register #(.width(18)) register_9 (.D(Input), .en(and_9_out), .Q(register_9_q), .clk(clk), .clr(1'b0));
  Register #(.width(18)) register_10 (.D(Input), .en(and_10_out), .Q(register_10_q), .clk(clk), .clr(1'b0));
  Register #(.width(18)) register_11 (.D(Input), .en(and_11_out), .Q(register_11_q), .clk(clk), .clr(1'b0));
  Register #(.width(18)) register_12 (.D(Input), .en(and_12_out), .Q(register_12_q), .clk(clk), .clr(1'b0));
  Register #(.width(18)) register_13 (.D(Input), .en(and_13_out), .Q(register_13_q), .clk(clk), .clr(1'b0));
  Register #(.width(18)) register_14 (.D(Input), .en(and_14_out), .Q(register_14_q), .clk(clk), .clr(1'b0));
  Register #(.width(18)) register_15 (.D(Input), .en(and_15_out), .Q(register_15_q), .clk(clk), .clr(1'b0));
  Register #(.width(18)) register_16 (.D(Input), .en(and_16_out), .Q(register_16_q), .clk(clk), .clr(1'b0));
  Multiplexer #(.select(4), .width(18), .enable("false")) multiplexer_1 (
    .in0(register_1_q), .in1(register_2_q), .in2(register_3_q), .in3(register_4_q), .in4(register_5_q),
    .in5(register_6_q), .in6(register_7_q), .in7(register_8_q), .in8(register_9_q), .in9(register_10_q),
    .in10(register_11_q), .in11(register_12_q), .in12(register_13_q), .in13(register_14_q),
    .in14(register_15_q), .in15(register_16_q), .out(Output1), .sel(undriven));
  Multiplexer #(.select(4), .width(18), .enable("false")) multiplexer_2 (
    .in0(register_1_q), .in1(register_2_q), .in2(register_3_q), .in3(register_4_q), .in4(register_5_q),
    .in5(register_6_q), .in6(register_7_q), .in7(register_8_q), .in8(register_9_q), .in9(register_10_q),
    .in10(register_11_q), .in11(register_12_q), .in12(register_13_q), .in13(register_14_q),
    .in14(register_15_q), .in15(register_16_q), .out(Output2), .sel(undriven_2));
endmodule

module ALU (
  input  [17:0] in1,
  input  [17:0] in2,
  input  [1:0] operation,
  output [17:0] out_data
);

  wire n18bitadder_1_cout;
  wire [17:0] and_1_out, n18bitadder_1_s0, or_1_out, xor_1_out;

  assign and_1_out = in1 & in2;  // AND_Gate and_1, 18 bits wide
  assign or_1_out = in1 | in2;  // OR_Gate or_1, 18 bits wide
  assign xor_1_out = in1 ^ in2;  // XOR_Gate xor_1, 18 bits wide
  Multiplexer #(.select(2), .width(18), .enable("false")) multiplexer_1 (
    .in0(n18bitadder_1_s0), .in1(and_1_out), .in2(or_1_out), .in3(xor_1_out), .out(out_data), .sel(operation));
  _18bitAdder u_18bitadder_1 (
    .b2(in2[2]), .b6(in2[6]), .b10(in2[10]), .b14(in2[14]), .a2(in1[2]), .a6(in1[6]), .a10(in1[10]),
    .a14(in1[14]), .b3(in2[3]), .b7(in2[7]), .b11(in2[11]), .b15(in2[15]), .a3(in1[3]), .a7(in1[7]),
    .a11(in1[11]), .a15(in1[15]), .b4(in2[4]), .b8(in2[8]), .b12(in2[12]), .b16(in2[16]), .a4(in1[4]),
    .a8(in1[8]), .a12(in1[12]), .a16(in1[16]), .Cout(n18bitadder_1_cout), .b5(in2[5]), .b9(in2[9]),
    .b13(in2[13]), .b17(in2[17]), .a5(in1[5]), .a9(in1[9]), .a13(in1[13]), .a17(in1[17]),
    .s0(n18bitadder_1_s0[0]), .s1(n18bitadder_1_s0[1]), .s17(n18bitadder_1_s0[17]), .s5(n18bitadder_1_s0[5]),
    .s9(n18bitadder_1_s0[6]), .s13(n18bitadder_1_s0[13]), .s16(n18bitadder_1_s0[16]),
    .s4(n18bitadder_1_s0[4]), .s8(n18bitadder_1_s0[7]), .s12(n18bitadder_1_s0[12]),
    .s15(n18bitadder_1_s0[15]), .s3(n18bitadder_1_s0[3]), .s7(n18bitadder_1_s0[8]),
    .s11(n18bitadder_1_s0[11]), .s14(n18bitadder_1_s0[14]), .s2(n18bitadder_1_s0[2]),
    .s6(n18bitadder_1_s0[9]), .s10(n18bitadder_1_s0[10]), .b0(in2[0]), .a0(in1[0]), .b1(in2[1]), .a1(in1[1]));
endmodule

module ControlUnit (
  input  [17:0] in_1,
  output SRC_MUX,
  output MEM_WRITE,
  output MEM_READ,
  output REG_WRITE,
  output ADDR
);

  wire ADD, ADDI, AND, ANDI, BEQ, BGE, BGT, BLE, BLT, JUMP, OR, ORI, XOR, XORI;

  Decoder #(.select(4), .enable("false")) decoder_1 (
    .out0(ADD), .out1(ADDI), .out2(AND), .out3(ANDI), .out4(OR), .out5(ORI), .out6(XOR), .out7(XORI),
    .out8(JUMP), .out9(MEM_READ), .out10(MEM_WRITE), .out11(BEQ), .out12(BLT), .out13(BLE), .out14(BGT),
    .out15(BGE), .sel(in_1[3:0]));
  or or_1 (SRC_MUX, ADD, AND, OR, XOR);
  or or_2 (REG_WRITE, ADD, ADDI, AND, ANDI, OR, ORI, XOR, XORI, MEM_READ);
  or or_3 (ADDR, BEQ, BLT, BLE, BGT, BGE, JUMP, MEM_READ, MEM_WRITE);

  // Other names for the same wires on the sheet: ADDRESS[9:0] = in_1[17:8]; JUMPADDRESS[13:0] = in_1[17:4];
  //   SRC1[3:0] = in_1[11:8]; BRANCHADDRESS[2:0] = in_1[17:15];
  //   IMM[17:0] = {{13{in_1[15]}}, in_1[14:12], in_1[17:16]}; SRC2[3:0] = in_1[15:12]; OPCODE[3:0] = in_1[3:0];
  //   DR[3:0] = in_1[7:4]; LD = MEM_READ; ST = MEM_WRITE
endmodule

// half adder
module halfAdder (
  input  A,
  input  B,
  output S,
  output Cout
);

  xor xor_1 (S, A, B);
  and and_1 (Cout, A, B);
endmodule

// full adder
module fullAdder (
  input  A,
  input  B,
  input  Cin,
  output S,
  output Cout
);

  wire and_1_out, and_2_out, xor_1_out;

  xor xor_1 (xor_1_out, A, B);
  xor xor_2 (S, xor_1_out, Cin);
  and and_1 (and_1_out, Cin, xor_1_out);
  and and_2 (and_2_out, B, A);
  or or_1 (Cout, and_1_out, and_2_out);
endmodule

// 4 bit full adder
module _4bitAdder (
  input  b0,
  input  a0,
  input  b1,
  input  a1,
  input  b2,
  input  a2,
  input  b3,
  input  a3,
  input  Cin,
  output co,
  output s0,
  output s1,
  output s2,
  output s3
);

  wire fulladder_1_cout, fulladder_2_cout, fulladder_3_cout;

  fullAdder fulladder_1 (.A(a0), .B(b0), .Cin(Cin), .S(s0), .Cout(fulladder_1_cout));
  fullAdder fulladder_2 (.A(a1), .B(b1), .Cin(fulladder_1_cout), .S(s1), .Cout(fulladder_2_cout));
  fullAdder fulladder_3 (.A(a2), .B(b2), .Cin(fulladder_2_cout), .S(s2), .Cout(fulladder_3_cout));
  fullAdder fulladder_4 (.A(a3), .B(b3), .Cin(fulladder_3_cout), .S(s3), .Cout(co));
endmodule

module _18bitAdder (
  input  b2,
  input  b6,
  input  b10,
  input  b14,
  input  a2,
  input  a6,
  input  a10,
  input  a14,
  input  b3,
  input  b7,
  input  b11,
  input  b15,
  input  a3,
  input  a7,
  input  a11,
  input  a15,
  input  b4,
  input  b8,
  input  b12,
  input  b16,
  input  a4,
  input  a8,
  input  a12,
  input  a16,
  input  b0,
  input  a0,
  input  b1,
  input  a1,
  input  b5,
  input  b9,
  input  b13,
  input  b17,
  input  a5,
  input  a9,
  input  a13,
  input  a17,
  output Cout,
  output s0,
  output s1,
  output s17,
  output s5,
  output s9,
  output s13,
  output s16,
  output s4,
  output s8,
  output s12,
  output s15,
  output s3,
  output s7,
  output s11,
  output s14,
  output s2,
  output s6,
  output s10
);

  wire fulladder_1_cout, halfadder_1_cout, n4bitadder_1_co, n4bitadder_2_co, n4bitadder_3_co;

  halfAdder halfadder_1 (.A(a0), .B(b0), .Cout(halfadder_1_cout), .S(s0));
  fullAdder fulladder_1 (.A(a1), .B(b1), .Cin(halfadder_1_cout), .S(s1), .Cout(fulladder_1_cout));
  _4bitAdder u_4bitadder_1 (
    .b0(b2), .a0(a2), .b1(b3), .a1(a3), .b2(b4), .a2(a4), .b3(b5), .a3(a5), .s0(s2), .s1(s3), .s2(s4),
    .s3(s5), .Cin(fulladder_1_cout), .co(n4bitadder_1_co));
  _4bitAdder u_4bitadder_2 (
    .b0(b6), .a0(a6), .b1(b7), .a1(a7), .b2(b8), .a2(a8), .b3(b9), .a3(a9), .s0(s6), .s1(s7), .s2(s8),
    .s3(s9), .Cin(n4bitadder_1_co), .co(n4bitadder_2_co));
  _4bitAdder u_4bitadder_3 (
    .b0(b10), .a0(a10), .b1(b11), .a1(a11), .b2(b12), .a2(a12), .b3(b13), .a3(a13), .s0(s10), .s1(s11),
    .s2(s12), .s3(s13), .Cin(n4bitadder_2_co), .co(n4bitadder_3_co));
  _4bitAdder u_4bitadder_4 (
    .b0(b14), .a0(a14), .b1(b15), .a1(a15), .b2(b16), .a2(a16), .b3(b17), .a3(a17), .s0(s14), .s1(s15),
    .s2(s16), .s3(s17), .Cin(n4bitadder_3_co), .co(Cout));
endmodule

// ControlUnit
module CU (
  input  [17:0] \input ,
  input  clk,
  output m1,
  output [1:0] alu_c,
  output m3,
  output Mem_r,
  output Mem_w,
  output m5,
  output branch,
  output WE,
  output [1:0] m2,
  output m4,
  output pc_w,
  output pc_r,
  output [3:0] DR,
  output [3:0] SRC1,
  output [3:0] SRC2,
  output [17:0] IMM,
  output [17:0] ADRESS,
  output [17:0] JUMPADRESS,
  output [2:0] mcmp,
  output [17:0] ADRESS_2
);

  wire and_2_out, and_3_out, and_5_out, decoder_1_out0, decoder_1_out1, decoder_1_out2, decoder_1_out3,
       decoder_1_out4, decoder_1_out5, decoder_1_out6, decoder_1_out7, decoder_1_out8, decoder_1_out9,
       decoder_1_out10, decoder_1_out11, decoder_1_out12, not_1_out, or_2_out, or_6_out, register_1_q;
  wire [3:0] counter_1_q;

  and and_1 (mcmp[0], ~\input [5], \input [3]);  // AND_Gate
  and and_2 (and_2_out, ~\input [5], \input [4], \input [3]);  // AND_Gate
  or or_1 (mcmp[1], and_2_out, and_3_out);
  and and_3 (and_3_out, \input [5], ~\input [3], ~\input [4]);  // AND_Gate
  and and_4 (mcmp[2], \input [4], \input [5], ~\input [3]);  // AND_Gate
  Counter #(.width(4), .max('hf)) counter_1 (
    .load(decoder_1_out1), .D(\input [17:14]), .count(or_2_out), .Q(counter_1_q), .clk(clk), .clr(and_5_out));  // open: carry
  and and_5 (and_5_out, not_1_out, register_1_q);
  not not_1 (not_1_out, or_2_out);
  Register #(.width(1)) register_1 (.D(pc_w), .en(1'b1), .Q(register_1_q), .clk(clk), .clr(1'b0));
  or or_2 (or_2_out, decoder_1_out0, decoder_1_out11);
  Multiplexer #(.width(4), .enable("false")) multiplexer_1 (
    .in0(\input [9:6]), .in1(\input [13:10]), .out(SRC1), .sel(Mem_w));
  Decoder #(.select(4), .enable("false")) decoder_1 (
    .out0(decoder_1_out0), .out1(decoder_1_out1), .out2(decoder_1_out2), .out3(decoder_1_out3),
    .out4(decoder_1_out4), .out5(decoder_1_out5), .out6(decoder_1_out6), .out7(decoder_1_out7),
    .out8(decoder_1_out8), .out9(decoder_1_out9), .out10(decoder_1_out10), .out11(decoder_1_out11),
    .out12(decoder_1_out12), .out13(Mem_w), .out14(branch), .sel(counter_1_q));  // open: out15
  assign IMM = {{12{\input [5]}}, \input [5:0]};  // Bit_Extender bit_extender_1
  assign ADRESS = {{8{1'b0}}, \input [9:0]};  // Bit_Extender bit_extender_2
  assign JUMPADRESS = {{4{1'b0}}, \input [13:0]};  // Bit_Extender bit_extender_3
  assign ADRESS_2 = {{15{1'b0}}, \input [2:0]};  // Bit_Extender bit_extender_4
  or or_3 (m1, decoder_1_out3, decoder_1_out5, decoder_1_out7, decoder_1_out9);
  or or_4 (alu_c[0], decoder_1_out4, decoder_1_out5, decoder_1_out8, decoder_1_out9);
  or or_5 (alu_c[1], decoder_1_out6, decoder_1_out7, decoder_1_out8, decoder_1_out9);
  or or_6 (or_6_out, decoder_1_out2, decoder_1_out3, decoder_1_out4, decoder_1_out5, decoder_1_out6, decoder_1_out7, decoder_1_out8, decoder_1_out9);
  or or_7 (m5, or_6_out, decoder_1_out11, decoder_1_out12, Mem_w);
  or or_8 (WE, or_6_out, decoder_1_out12);
  or or_9 (m2[0], decoder_1_out11, Mem_w, branch, decoder_1_out12);
  or or_10 (m2[1], branch, decoder_1_out10);
  or or_11 (pc_w, or_6_out, decoder_1_out12, Mem_w, branch);
  or or_12 (m3, or_6_out, decoder_1_out10, branch);
  or or_13 (Mem_r, decoder_1_out12, decoder_1_out11);

  assign DR = \input [13:10];
  assign m4 = 1'b0;
  assign pc_r = 1'b1;
  assign SRC2 = \input [5:2];

  // Other names for the same wires on the sheet: BRANCHADDRESS[17:0] = ADRESS_2; JUMPADDRESS[17:0] = JUMPADRESS;
  //   MEMADDRESS[17:0] = ADRESS

  // Notes on the sheet:
  //   F1
  //   F2
  //   ADD
  //   AND
  //   XOR
  //   JUMP
  //   LD1
  //   LD2
  //   ST
  //   BR
  //   OR
endmodule

module _1bitcomparator (
  input  a,
  input  b,
  input  eq_in,
  input  gt_in,
  input  lt_in,
  output eq_out,
  output gt_out,
  output lt_out
);

  wire and_1_out, and_2_out, not_1_out, not_2_out, xnor_1_out;

  not not_1 (not_1_out, b);
  not not_2 (not_2_out, a);
  xnor xnor_1 (xnor_1_out, a, b);
  and and_1 (and_1_out, a, eq_in, not_1_out);
  and and_2 (and_2_out, eq_in, not_2_out, b);
  and and_3 (eq_out, xnor_1_out, eq_in);
  or or_1 (gt_out, and_1_out, gt_in);
  or or_2 (lt_out, and_2_out, lt_in);
endmodule

module _4bitcomparator (
  input  a1,
  input  a2,
  input  a0,
  input  a3,
  input  b1,
  input  b0,
  input  b3,
  input  b2,
  input  eq_in,
  input  gt_in,
  input  lt_in,
  output eq_out,
  output gt_out,
  output lt_out
);

  wire n1bitcomparator_1_eq_out, n1bitcomparator_1_gt_out, n1bitcomparator_1_lt_out,
       n1bitcomparator_2_eq_out, n1bitcomparator_2_gt_out, n1bitcomparator_2_lt_out,
       n1bitcomparator_3_eq_out, n1bitcomparator_3_gt_out, n1bitcomparator_3_lt_out;

  _1bitcomparator u_1bitcomparator_1 (
    .a(a3), .b(b3), .eq_in(eq_in), .gt_in(gt_in), .lt_in(lt_in), .eq_out(n1bitcomparator_1_eq_out),
    .gt_out(n1bitcomparator_1_gt_out), .lt_out(n1bitcomparator_1_lt_out));
  _1bitcomparator u_1bitcomparator_2 (
    .a(a2), .b(b2), .eq_in(n1bitcomparator_1_eq_out), .gt_in(n1bitcomparator_1_gt_out),
    .lt_in(n1bitcomparator_1_lt_out), .eq_out(n1bitcomparator_2_eq_out), .gt_out(n1bitcomparator_2_gt_out),
    .lt_out(n1bitcomparator_2_lt_out));
  _1bitcomparator u_1bitcomparator_3 (
    .a(a1), .b(b1), .eq_in(n1bitcomparator_2_eq_out), .gt_in(n1bitcomparator_2_gt_out),
    .lt_in(n1bitcomparator_2_lt_out), .eq_out(n1bitcomparator_3_eq_out), .gt_out(n1bitcomparator_3_gt_out),
    .lt_out(n1bitcomparator_3_lt_out));
  _1bitcomparator u_1bitcomparator_4 (
    .a(a0), .b(b0), .eq_in(n1bitcomparator_3_eq_out), .gt_in(n1bitcomparator_3_gt_out),
    .lt_in(n1bitcomparator_3_lt_out), .eq_out(eq_out), .gt_out(gt_out), .lt_out(lt_out));
endmodule

// Comparator
module _18bitcomparator (
  input  [17:0] in2,
  input  [17:0] in1,
  output eq_out,
  output gt_out,
  output lt_out,
  output ge_out,
  output le_out
);

  wire n1bitcomparator_1_eq_out, n1bitcomparator_1_gt_out, n1bitcomparator_1_lt_out,
       n1bitcomparator_2_gt_out, n1bitcomparator_2_lt_out, n4bitcomparator_1_eq_out,
       n4bitcomparator_1_gt_out, n4bitcomparator_1_lt_out, n4bitcomparator_2_eq_out,
       n4bitcomparator_2_gt_out, n4bitcomparator_2_lt_out, n4bitcomparator_3_eq_out,
       n4bitcomparator_3_gt_out, n4bitcomparator_3_lt_out, n4bitcomparator_4_eq_out,
       n4bitcomparator_4_gt_out, n4bitcomparator_4_lt_out, not_1_out, not_2_out, xor_1_out;

  _4bitcomparator u_4bitcomparator_1 (
    .a1(in1[14]), .a2(in1[15]), .a0(in1[16]), .a3(in1[17]), .b1(in2[14]), .b0(in2[15]), .b3(in2[16]),
    .b2(in2[17]), .eq_in(1'b1), .gt_in(1'b0), .lt_in(1'b0), .eq_out(n4bitcomparator_1_eq_out),
    .gt_out(n4bitcomparator_1_gt_out), .lt_out(n4bitcomparator_1_lt_out));
  _4bitcomparator u_4bitcomparator_2 (
    .a1(in1[10]), .a2(in1[11]), .a0(in1[12]), .a3(in1[13]), .b1(in2[10]), .b0(in2[11]), .b3(in2[12]),
    .b2(in2[13]), .eq_in(n4bitcomparator_1_eq_out), .gt_in(n4bitcomparator_1_gt_out),
    .lt_in(n4bitcomparator_1_lt_out), .eq_out(n4bitcomparator_2_eq_out), .gt_out(n4bitcomparator_2_gt_out),
    .lt_out(n4bitcomparator_2_lt_out));
  _4bitcomparator u_4bitcomparator_3 (
    .a1(in1[6]), .a2(in1[7]), .a0(in1[8]), .a3(in1[9]), .b1(in2[6]), .b0(in2[7]), .b3(in2[8]), .b2(in2[9]),
    .eq_in(n4bitcomparator_2_eq_out), .gt_in(n4bitcomparator_2_gt_out), .lt_in(n4bitcomparator_2_lt_out),
    .eq_out(n4bitcomparator_3_eq_out), .gt_out(n4bitcomparator_3_gt_out), .lt_out(n4bitcomparator_3_lt_out));
  _4bitcomparator u_4bitcomparator_4 (
    .a1(in1[2]), .a2(in1[3]), .a0(in1[4]), .a3(in1[5]), .b1(in2[2]), .b0(in2[3]), .b3(in2[4]), .b2(in2[5]),
    .eq_in(n4bitcomparator_3_eq_out), .gt_in(n4bitcomparator_3_gt_out), .lt_in(n4bitcomparator_3_lt_out),
    .eq_out(n4bitcomparator_4_eq_out), .gt_out(n4bitcomparator_4_gt_out), .lt_out(n4bitcomparator_4_lt_out));
  _1bitcomparator u_1bitcomparator_1 (
    .a(in2[1]), .b(in1[1]), .eq_in(n4bitcomparator_4_eq_out), .gt_in(n4bitcomparator_4_gt_out),
    .lt_in(n4bitcomparator_4_lt_out), .eq_out(n1bitcomparator_1_eq_out), .gt_out(n1bitcomparator_1_gt_out),
    .lt_out(n1bitcomparator_1_lt_out));
  xor xor_1 (xor_1_out, in2[17], in1[17]);
  Multiplexer #(.enable("false")) multiplexer_1 (
    .in0(n1bitcomparator_2_gt_out), .in1(not_1_out), .out(gt_out), .sel(xor_1_out));
  not not_1 (not_1_out, n1bitcomparator_2_gt_out);
  Multiplexer #(.enable("false")) multiplexer_2 (
    .in0(n1bitcomparator_2_lt_out), .in1(not_2_out), .out(lt_out), .sel(xor_1_out));
  not not_2 (not_2_out, n1bitcomparator_2_lt_out);
  _1bitcomparator u_1bitcomparator_2 (
    .a(in1[0]), .b(in2[0]), .eq_in(n1bitcomparator_1_eq_out), .gt_in(n1bitcomparator_1_gt_out),
    .lt_in(n1bitcomparator_1_lt_out), .eq_out(eq_out), .gt_out(n1bitcomparator_2_gt_out),
    .lt_out(n1bitcomparator_2_lt_out));
  or or_1 (ge_out, gt_out, eq_out);
  or or_2 (le_out, lt_out, eq_out);
endmodule

// RegisterFile
module RegFile (
  input  [3:0] SRC1,
  input  [17:0] Input,
  input  [3:0] SRC2,
  input  [3:0] DR,
  input  WE,
  input  clk,
  output [17:0] Output1,
  output [17:0] Output2
);

  wire and_1_out, and_2_out, and_3_out, and_4_out, and_5_out, and_6_out, and_7_out, and_8_out, and_9_out,
       and_10_out, and_11_out, and_12_out, and_13_out, and_14_out, and_15_out, and_16_out, decoder_1_out0,
       decoder_1_out1, decoder_1_out2, decoder_1_out3, decoder_1_out4, decoder_1_out5, decoder_1_out6,
       decoder_1_out7, decoder_1_out8, decoder_1_out9, decoder_1_out10, decoder_1_out11, decoder_1_out12,
       decoder_1_out13, decoder_1_out14, decoder_1_out15, decoder_2_out0, decoder_2_out1, decoder_2_out2,
       decoder_2_out3, decoder_2_out4, decoder_2_out5, decoder_2_out6, decoder_2_out7, decoder_2_out8,
       decoder_2_out9, decoder_2_out10, decoder_2_out11, decoder_2_out12, decoder_2_out13, decoder_2_out14,
       decoder_2_out15, decoder_3_out0, decoder_3_out1, decoder_3_out2, decoder_3_out3, decoder_3_out4,
       decoder_3_out5, decoder_3_out6, decoder_3_out7, decoder_3_out8, decoder_3_out9, decoder_3_out10,
       decoder_3_out11, decoder_3_out12, decoder_3_out13, decoder_3_out14, decoder_3_out15;
  wire [17:0] register_1_q, register_2_q, register_3_q, register_4_q, register_5_q, register_6_q,
       register_7_q, register_8_q, register_9_q, register_10_q, register_11_q, register_12_q, register_13_q,
       register_14_q, register_15_q, register_16_q;

  Decoder #(.select(4), .enable("false")) decoder_1 (
    .out0(decoder_1_out0), .out1(decoder_1_out1), .out2(decoder_1_out2), .out3(decoder_1_out3),
    .out4(decoder_1_out4), .out5(decoder_1_out5), .out6(decoder_1_out6), .out7(decoder_1_out7),
    .out8(decoder_1_out8), .out9(decoder_1_out9), .out10(decoder_1_out10), .out11(decoder_1_out11),
    .out12(decoder_1_out12), .out13(decoder_1_out13), .out14(decoder_1_out14), .out15(decoder_1_out15),
    .sel(SRC1));
  Decoder #(.select(4), .enable("false")) decoder_2 (
    .out0(decoder_2_out0), .out1(decoder_2_out1), .out2(decoder_2_out2), .out3(decoder_2_out3),
    .out4(decoder_2_out4), .out5(decoder_2_out5), .out6(decoder_2_out6), .out7(decoder_2_out7),
    .out8(decoder_2_out8), .out9(decoder_2_out9), .out10(decoder_2_out10), .out11(decoder_2_out11),
    .out12(decoder_2_out12), .out13(decoder_2_out13), .out14(decoder_2_out14), .out15(decoder_2_out15),
    .sel(SRC2));
  Decoder #(.select(4), .enable("false")) decoder_3 (
    .out0(decoder_3_out0), .out1(decoder_3_out1), .out2(decoder_3_out2), .out3(decoder_3_out3),
    .out4(decoder_3_out4), .out5(decoder_3_out5), .out6(decoder_3_out6), .out7(decoder_3_out7),
    .out8(decoder_3_out8), .out9(decoder_3_out9), .out10(decoder_3_out10), .out11(decoder_3_out11),
    .out12(decoder_3_out12), .out13(decoder_3_out13), .out14(decoder_3_out14), .out15(decoder_3_out15),
    .sel(DR));
  and and_1 (and_1_out, decoder_3_out0, WE);
  and and_2 (and_2_out, decoder_3_out1, WE);
  and and_3 (and_3_out, decoder_3_out2, WE);
  and and_4 (and_4_out, decoder_3_out3, WE);
  and and_5 (and_5_out, decoder_3_out4, WE);
  and and_6 (and_6_out, decoder_3_out5, WE);
  and and_7 (and_7_out, decoder_3_out6, WE);
  and and_8 (and_8_out, decoder_3_out7, WE);
  and and_9 (and_9_out, decoder_3_out8, WE);
  and and_10 (and_10_out, decoder_3_out9, WE);
  and and_11 (and_11_out, decoder_3_out10, WE);
  and and_12 (and_12_out, decoder_3_out11, WE);
  and and_13 (and_13_out, decoder_3_out12, WE);
  and and_14 (and_14_out, decoder_3_out13, WE);
  and and_15 (and_15_out, decoder_3_out14, WE);
  and and_16 (and_16_out, decoder_3_out15, WE);
  Register #(.width(18)) register_1 (.D(Input), .en(and_1_out), .Q(register_1_q), .clk(clk), .clr(1'b0));
  Register #(.width(18)) register_2 (.D(Input), .en(and_2_out), .Q(register_2_q), .clk(clk), .clr(1'b0));
  Register #(.width(18)) register_3 (.D(Input), .en(and_3_out), .Q(register_3_q), .clk(clk), .clr(1'b0));
  Register #(.width(18)) register_4 (.D(Input), .en(and_4_out), .Q(register_4_q), .clk(clk), .clr(1'b0));
  Register #(.width(18)) register_5 (.D(Input), .en(and_5_out), .Q(register_5_q), .clk(clk), .clr(1'b0));
  Register #(.width(18)) register_6 (.D(Input), .en(and_6_out), .Q(register_6_q), .clk(clk), .clr(1'b0));
  Register #(.width(18)) register_7 (.D(Input), .en(and_7_out), .Q(register_7_q), .clk(clk), .clr(1'b0));
  Register #(.width(18)) register_8 (.D(Input), .en(and_8_out), .Q(register_8_q), .clk(clk), .clr(1'b0));
  Register #(.width(18)) register_9 (.D(Input), .en(and_9_out), .Q(register_9_q), .clk(clk), .clr(1'b0));
  Register #(.width(18)) register_10 (.D(Input), .en(and_10_out), .Q(register_10_q), .clk(clk), .clr(1'b0));
  Register #(.width(18)) register_11 (.D(Input), .en(and_11_out), .Q(register_11_q), .clk(clk), .clr(1'b0));
  Register #(.width(18)) register_12 (.D(Input), .en(and_12_out), .Q(register_12_q), .clk(clk), .clr(1'b0));
  Register #(.width(18)) register_13 (.D(Input), .en(and_13_out), .Q(register_13_q), .clk(clk), .clr(1'b0));
  Register #(.width(18)) register_14 (.D(Input), .en(and_14_out), .Q(register_14_q), .clk(clk), .clr(1'b0));
  Register #(.width(18)) register_15 (.D(Input), .en(and_15_out), .Q(register_15_q), .clk(clk), .clr(1'b0));
  Register #(.width(18)) register_16 (.D(Input), .en(and_16_out), .Q(register_16_q), .clk(clk), .clr(1'b0));
  assign Output1 = decoder_1_out0 ? register_1_q : 18'bz;  // Controlled_Buffer controlled_buffer_1
  assign Output1 = decoder_1_out1 ? register_2_q : 18'bz;  // Controlled_Buffer controlled_buffer_2
  assign Output1 = decoder_1_out2 ? register_3_q : 18'bz;  // Controlled_Buffer controlled_buffer_3
  assign Output1 = decoder_1_out3 ? register_4_q : 18'bz;  // Controlled_Buffer controlled_buffer_4
  assign Output1 = decoder_1_out4 ? register_5_q : 18'bz;  // Controlled_Buffer controlled_buffer_5
  assign Output1 = decoder_1_out5 ? register_6_q : 18'bz;  // Controlled_Buffer controlled_buffer_6
  assign Output1 = decoder_1_out6 ? register_7_q : 18'bz;  // Controlled_Buffer controlled_buffer_7
  assign Output1 = decoder_1_out7 ? register_8_q : 18'bz;  // Controlled_Buffer controlled_buffer_8
  assign Output1 = decoder_1_out8 ? register_9_q : 18'bz;  // Controlled_Buffer controlled_buffer_9
  assign Output1 = decoder_1_out9 ? register_10_q : 18'bz;  // Controlled_Buffer controlled_buffer_10
  assign Output1 = decoder_1_out10 ? register_11_q : 18'bz;  // Controlled_Buffer controlled_buffer_11
  assign Output1 = decoder_1_out11 ? register_12_q : 18'bz;  // Controlled_Buffer controlled_buffer_12
  assign Output1 = decoder_1_out12 ? register_13_q : 18'bz;  // Controlled_Buffer controlled_buffer_13
  assign Output1 = decoder_1_out13 ? register_14_q : 18'bz;  // Controlled_Buffer controlled_buffer_14
  assign Output1 = decoder_1_out14 ? register_15_q : 18'bz;  // Controlled_Buffer controlled_buffer_15
  assign Output1 = decoder_1_out15 ? register_16_q : 18'bz;  // Controlled_Buffer controlled_buffer_16
  assign Output2 = decoder_2_out0 ? register_1_q : 18'bz;  // Controlled_Buffer controlled_buffer_17
  assign Output2 = decoder_2_out1 ? register_2_q : 18'bz;  // Controlled_Buffer controlled_buffer_18
  assign Output2 = decoder_2_out2 ? register_3_q : 18'bz;  // Controlled_Buffer controlled_buffer_19
  assign Output2 = decoder_2_out3 ? register_4_q : 18'bz;  // Controlled_Buffer controlled_buffer_20
  assign Output2 = decoder_2_out4 ? register_5_q : 18'bz;  // Controlled_Buffer controlled_buffer_21
  assign Output2 = decoder_2_out5 ? register_6_q : 18'bz;  // Controlled_Buffer controlled_buffer_22
  assign Output2 = decoder_2_out6 ? register_7_q : 18'bz;  // Controlled_Buffer controlled_buffer_23
  assign Output2 = decoder_2_out7 ? register_8_q : 18'bz;  // Controlled_Buffer controlled_buffer_24
  assign Output2 = decoder_2_out8 ? register_9_q : 18'bz;  // Controlled_Buffer controlled_buffer_25
  assign Output2 = decoder_2_out9 ? register_10_q : 18'bz;  // Controlled_Buffer controlled_buffer_26
  assign Output2 = decoder_2_out10 ? register_11_q : 18'bz;  // Controlled_Buffer controlled_buffer_27
  assign Output2 = decoder_2_out11 ? register_12_q : 18'bz;  // Controlled_Buffer controlled_buffer_28
  assign Output2 = decoder_2_out12 ? register_13_q : 18'bz;  // Controlled_Buffer controlled_buffer_29
  assign Output2 = decoder_2_out13 ? register_14_q : 18'bz;  // Controlled_Buffer controlled_buffer_30
  assign Output2 = decoder_2_out14 ? register_15_q : 18'bz;  // Controlled_Buffer controlled_buffer_31
  assign Output2 = decoder_2_out15 ? register_16_q : 18'bz;  // Controlled_Buffer controlled_buffer_32
endmodule
